# Fritzing sketch Untitled Sketch (saved by Fritzing 0.9.3b)
breadboards: 1

parts:
  Adafruit_HUZZAH_ESP8266_Breakout1 = Adafruit HUZZAH ESP8266 Breakout [part_number=2471]
  BREAKOUT1 = MAX31850 Thermocouple Breakout
  BREAKOUT2 = MAX31850 Thermocouple Breakout
  R1 = Resistor [tolerance=±5% resistance=4.7k package=THT]  # not connected

nets:
  N1: Adafruit_HUZZAH_ESP8266_Breakout1.#4, BREAKOUT1.DATA, BREAKOUT2.DATA
  N2: Adafruit_HUZZAH_ESP8266_Breakout1.#15, Adafruit_HUZZAH_ESP8266_Breakout1.3V
  GND: BREAKOUT1.GND, BREAKOUT1.VIN
