# Fritzing sketch schmatic (saved by Fritzing 0.9.3b)
circuit board: 8.46667cm x 5.64444cm
breadboards: 1

parts:
  Part1 = Adafruit HUZZAH ESP8266 [part_number="Adafruit #2471"]
  BREAKOUT1 = MAX31850 Thermocouple Breakout
  BREAKOUT2 = MAX31850 Thermocouple Breakout
  R1 = Resistor [tolerance=±5% resistance=220 package=THT]
  M1 = DC Motor
  Q1 = TIP120 Hi-Current Darlington Transistor
  R2 = Resistor [tolerance=±5% resistance=220 package=THT]
  D1 = Rectifier Diode [part_number=1N4001 package="300 mil [THT]"]
  U1 = Voltage Regulator - 5V [package="TO220 [THT]"]
  BREAKOUT3 = MAX31850 Thermocouple Breakout

nets:
  N1: Part1.VBAT, U1.input_voltage
  GND: Part1.GND, BREAKOUT1.GND, BREAKOUT2.GND, Q1.EMITTER, U1.output_voltage, BREAKOUT3.GND
  VIN: Part1.3.3V, BREAKOUT1.VIN, BREAKOUT2.VIN, R1.Pin_1, BREAKOUT3.VIN
  N2: Part1.GPIO15, R2.Pin_1
  N3: Part1.GPIO4, BREAKOUT1.DATA, BREAKOUT2.DATA, R1.Pin_0, BREAKOUT3.DATA
  N4: M1.pin_1, Q1.COLLECTOR, D1.cathode
  N5: M1.pin_2, U1.GND
  N6: Q1.BASE, R2.Pin_0

custom parts:
  Adafruit HUZZAH ESP8266: Add Internet to your next project with an adorable, bite-sized WiFi microcontroller, at a price you like! The ESP8266 processor from Espressif is an 80 MHz microcontroller with a full WiFi front-end (both as client and access point) and TCP/IP stack with DNS support as well. While this chip has been very popular, its also been very difficult to use. Most of the low cost modules are not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
